// Logisim project SPM.circ as structural Verilog: 4 circuits, main circuit main
module main (
  input  y__serial_in,
  input  x0,
  input  x1,
  input  x2,
  input  p3,
  input  p2,
  input  x3,
  input  p1,
  input  p0,
  input  x4,
  input  p7,
  input  x5,
  input  x6,
  input  x7,
  input  in_15,
  output serial_output
);

  wire and_1_out, and_2_out, and_3_out, and_4_out, and_5_out, and_6_out, and_7_out, and_8_out, clock_1_out,
       csadd_2_sum, csadd_3_sum, csadd_4_sum, csadd_5_sum, csadd_6_sum, csadd_7_sum, tcmp_1_out_4,
       unit_digit_1_a, unit_digit_1_b, unit_digit_1_c, unit_digit_1_d, unit_digit_1_e, unit_digit_1_f,
       unit_digit_1_g;

  Clock clock_1 (.out(clock_1_out));
  and and_1 (and_1_out, x0, y__serial_in);
  and and_2 (and_2_out, x1, y__serial_in);
  and and_3 (and_3_out, x2, y__serial_in);
  and and_4 (and_4_out, x3, y__serial_in);
  and and_5 (and_5_out, x4, y__serial_in);
  and and_6 (and_6_out, x5, x5, y__serial_in);
  and and_7 (and_7_out, x6, y__serial_in);
  and and_8 (and_8_out, x7, y__serial_in);
  CSADD csadd_1 (.X(and_1_out), .Y(csadd_2_sum), .SUM(serial_output), .rst(in_15), .clk(clock_1_out));
  CSADD csadd_2 (.X(and_2_out), .Y(csadd_3_sum), .SUM(csadd_2_sum), .rst(in_15), .clk(clock_1_out));
  CSADD csadd_3 (.X(and_3_out), .Y(csadd_4_sum), .SUM(csadd_3_sum), .rst(in_15), .clk(clock_1_out));
  CSADD csadd_4 (.X(and_4_out), .Y(csadd_5_sum), .SUM(csadd_4_sum), .rst(in_15), .clk(clock_1_out));
  CSADD csadd_5 (.X(and_5_out), .Y(csadd_6_sum), .SUM(csadd_5_sum), .rst(in_15), .clk(clock_1_out));
  CSADD csadd_6 (.X(and_6_out), .Y(csadd_7_sum), .SUM(csadd_6_sum), .rst(in_15), .clk(clock_1_out));
  CSADD csadd_7 (.X(and_7_out), .Y(tcmp_1_out_4), .SUM(csadd_7_sum), .rst(in_15), .clk(clock_1_out));
  TCMP tcmp_1 (.A(and_8_out), .reset(in_15), .out_4(tcmp_1_out_4), .clk(clock_1_out));
  unit_digit unit_digit_1 (
    .p3(p3), .p2(p2), .p1(p1), .p0(p0), .a(unit_digit_1_a), .b(unit_digit_1_b), .c(unit_digit_1_c),
    .d(unit_digit_1_d), .e(unit_digit_1_e), .f(unit_digit_1_f), .g(unit_digit_1_g));
  _7_Segment_Display u_7_segment_display_1 (.g(p7));  // open: f, a, b, e, d, c, dp
  _7_Segment_Display u_7_segment_display_2 (
    .g(unit_digit_1_g), .f(unit_digit_1_f), .a(unit_digit_1_a), .b(unit_digit_1_b), .e(unit_digit_1_e),
    .d(unit_digit_1_d), .c(unit_digit_1_c));  // open: dp

  // Notes on the sheet:
  //   reset
  //   clk
endmodule

module CSADD (
  input  X,
  input  Y,
  input  clk,
  input  rst,
  output SUM
);

  wire adder_1_cout, adder_1_out, and_1_out, and_2_out, d_ff_2_q, not_1_out, xor_1_out, xor_2_out;

  Adder #(.width(1)) adder_1 (.a(Y), .b(d_ff_2_q), .out(adder_1_out), .cin(1'b0), .cout(adder_1_cout));
  not not_1 (not_1_out, rst);
  and and_1 (and_1_out, X, adder_1_out);
  xor xor_1 (xor_1_out, X, adder_1_out);
  D_Flip_Flop #(.trigger("high")) d_ff_1 (
    .clk(clk), .D(xor_1_out), .Q(SUM), .reset(not_1_out));  // open: Qn, preset, en
  and and_2 (and_2_out, and_1_out, adder_1_cout);
  xor xor_2 (xor_2_out, and_1_out, adder_1_cout);
  D_Flip_Flop #(.trigger("high")) d_ff_2 (
    .clk(clk), .D(xor_2_out), .Q(d_ff_2_q), .reset(not_1_out));  // open: Qn, preset, en

  // Notes on the sheet:
  //   FDHA
  //   HSUM1
  //   CAR1
  //   FDHA
  //   SC
endmodule

module TCMP (
  input  A,
  input  clk,
  input  reset,
  output out_4
);

  wire d_ff_2_q, FDHA_out, not_1_out, or_1_out, xor_1_out;

  not not_1 (not_1_out, reset);
  and FDHA (FDHA_out, A, d_ff_2_q);
  xor xor_1 (xor_1_out, A, d_ff_2_q);
  D_Flip_Flop #(.trigger("high")) d_ff_1 (
    .clk(clk), .D(xor_1_out), .Q(out_4), .reset(not_1_out));  // open: Qn, preset, en
  or or_1 (or_1_out, A, d_ff_2_q);
  D_Flip_Flop #(.trigger("high")) d_ff_2 (
    .clk(clk), .D(or_1_out), .Q(d_ff_2_q), .reset(not_1_out));  // open: Qn, preset, en
endmodule

module unit_digit (
  input  p3,
  input  p2,
  input  p1,
  input  p0,
  output a,
  output b,
  output c,
  output d,
  output e,
  output f,
  output g
);

  wire and_1_out, and_2_out, and_3_out, and_4_out, and_5_out, and_6_out, and_7_out, and_8_out, and_9_out,
       and_10_out, and_11_out, and_12_out, and_13_out, and_14_out, and_15_out, and_16_out, not_1_out,
       not_2_out, not_3_out, not_4_out, not_5_out, not_6_out, not_7_out, not_8_out, not_9_out, not_10_out,
       not_11_out, not_12_out, not_13_out, not_14_out, not_15_out, not_16_out, not_17_out, not_18_out,
       not_19_out, not_20_out, not_21_out;

  not not_1 (not_1_out, p2);
  and and_1 (and_1_out, not_1_out, not_2_out);
  not not_2 (not_2_out, p0);
  and and_2 (and_2_out, p2, p0);
  not not_3 (not_3_out, p2);
  not not_4 (not_4_out, p1);
  and and_3 (and_3_out, not_4_out, not_5_out);
  not not_5 (not_5_out, p0);
  and and_4 (and_4_out, p1, p0);
  not not_6 (not_6_out, p1);
  or or_1 (c, not_6_out, p0, p2);
  not not_7 (not_7_out, p2);
  and and_5 (and_5_out, not_7_out, not_8_out);
  not not_8 (not_8_out, p0);
  not not_9 (not_9_out, p2);
  and and_6 (and_6_out, not_9_out, p1);
  and and_7 (and_7_out, p1, not_10_out);
  not not_10 (not_10_out, p0);
  and and_8 (and_8_out, p2, not_11_out, p0);
  not not_11 (not_11_out, p1);
  not not_12 (not_12_out, p2);
  and and_9 (and_9_out, not_12_out, not_13_out);
  not not_13 (not_13_out, p0);
  and and_10 (and_10_out, p1, not_14_out);
  not not_14 (not_14_out, p0);
  not not_15 (not_15_out, p1);
  and and_11 (and_11_out, not_15_out, not_16_out);
  not not_16 (not_16_out, p0);
  and and_12 (and_12_out, p2, not_17_out);
  not not_17 (not_17_out, p1);
  and and_13 (and_13_out, p2, not_18_out);
  not not_18 (not_18_out, p0);
  not not_19 (not_19_out, p2);
  and and_14 (and_14_out, not_19_out, p1);
  and and_15 (and_15_out, p2, not_20_out);
  not not_20 (not_20_out, p1);
  and and_16 (and_16_out, p2, not_21_out);
  not not_21 (not_21_out, p0);
  or or_2 (a, and_1_out, p1, and_2_out, p3);
  or or_3 (b, not_3_out, and_3_out, and_4_out);
  or or_4 (d, and_5_out, and_6_out, and_7_out, and_8_out, p3);
  or or_5 (e, and_9_out, and_10_out);
  or or_6 (f, and_11_out, and_12_out, and_13_out, p3);
  or or_7 (g, and_14_out, and_15_out, and_16_out, p3);
endmodule
